# Fritzing sketch PowerSupply (saved by Fritzing 0.9.3b)
circuit board: 1.14896cm x 1.98663cm
stripboards: 1

parts:
  J1 = female pin header, 2 pins [form="♀ (female)"]
  R1 = Resistor [tolerance=±5% resistance=470k part_number=R2 package=THT]
  R2 = Resistor [tolerance=±5% resistance=1M part_number=R1 package=THT]
  C1 = Ceramic Capacitor [capacitance=10nF part_number=R1 package="100 mil [THT, multilayer]"]
  J2 = female pin header, 3 pins [form="♀ (female)"]
  C2 = Ceramic Capacitor [capacitance=10nF part_number=C2 package="100 mil [THT, multilayer]"]

nets:
  N1: J1.pin1, R1.Pin_0, C1.0, J2.pin3, C2.1
  N2: J1.pin2, R2.Pin_0, C1.1
  N3: R1.Pin_1, R2.Pin_1, J2.pin2
  N4: J2.pin1, C2.0

notes:
  Vin
  GND
  3V3
  MEAS
