# Fritzing sketch PowerSupply_2 (saved by Fritzing 0.9.3b)

parts:
  U4 = V_REG_MIC5235 [part_number=TLV700 package=sot23-5]
  U8 = NPN_PNP Transistor Array [part_number=TPL5110 package=sot23-6]
  J1 = female pin header, 2 pins [form="♀ (female)" part_number=JST]
  S1 = Toggle Switch [part_number="Power switch" package=THT]
  R1 = Resistor [tolerance=±5% resistance=22k package=THT]
  C1 = Ceramic Capacitor [capacitance=100nF package="100 mil [THT, multilayer]"]
  C2 = Ceramic Capacitor [capacitance=100nF package="100 mil [THT, multilayer]"]
  J2 = female pin header, 3 pins [form="♀ (female)"]
  SJ1 = Solder Jumper [package=sj_2s]

nets:
  N1: U4.IN, U8.C2, S1.L2, C1.1, SJ1.1
  N2: U4.GND, U4.ADJ, U8.B2, J1.pin2, R1.Pin_0, C1.0, C2.0, J2.pin3
  N3: U4.EN, U8.B1, SJ1.2
  N4: U4.OUT, C2.1, J2.pin2
  N5: U8.C1, R1.Pin_1
  N6: U8.E1, J2.pin1
  N7: J1.pin1, S1.COM
